# Fritzing sketch Sensor Tem Umedad (saved by Fritzing 0.9.3b)
circuit board: 4.80622cm x 5.02281cm
breadboards: 1

parts:
  DHT1 = DHT11 Humitidy and Temperature Sensor
  J5 = Screw terminal - 2 pins [package=THT]
  R1 = Resistor [tolerance=±5% resistance=330 package=THT]
  U2 = MAX485 Breakout [chip_label=? package=THT]
  LED1 = smd LED [color="Green (565nm)" package="0805 [SMD]"]
  R2 = Resistor [tolerance=±5% resistance=330 package=THT]
  Componente1 = Arduino Nano (Rev3.0)
  C2 = Electrolytic Capacitor [capacitance=1µF package="100 mil [THT, electrolytic]"]

nets:
  VDD: DHT1.VDD, R1.Pin_1, U2.VCC, Componente1.5V
  N1: DHT1.DATA, R1.Pin_0, Componente1.D2
  GND: DHT1.GND, J5.pin1, U2.GND, LED1.cathode, Componente1.GND, C2.-
  N2: J5.pin2, Componente1.VIN, C2.+
  N3: U2.RO, Componente1.D3
  N4: U2.RE, U2.DE, Componente1.D7
  N5: U2.DI, Componente1.D4
  N6: LED1.anode, R2.Pin_1
  N7: R2.Pin_0, Componente1.D8

custom parts:
  DHT11 Humitidy and Temperature Sensor: DHT11 Humidity and Temperature Sensor
  MAX485 Breakout: MAX485 RS485 breakout board
